// Logisim project cpu.circ as structural Verilog: 5 circuits, main circuit main
module main (
  input  [31:0] INSTRUCTION,
  input  CLOCK,
  output [31:0] PROGRAM_COUNTER,
  output [31:0] ra,
  output [31:0] sp,
  output [31:0] t0,
  output [31:0] t1,
  output [31:0] t2,
  output [31:0] s0,
  output [31:0] s1,
  output [31:0] a0
);

  wire DMEM_p1, DMEM_p6, DMEM_p8;
  wire [31:0] alu, DMEM_p9, immediate_generator_1_immout, multiplexer_1_out, multiplexer_2_out,
       multiplexer_3_out, multiplexer_4_out, pc_plus_4, RegFile_read_data_1, RegFile_read_data_2,
       register_1_q;

  Adder #(.width(32)) adder_1 (.a(PROGRAM_COUNTER), .b(32'h4), .out(pc_plus_4));  // open: cin, cout
  Multiplexer #(.width(32), .enable("false")) multiplexer_1 (
    .in0(pc_plus_4), .in1(alu), .out(multiplexer_1_out));  // open: sel
  Register #(.width(32)) PC (.D(multiplexer_1_out), .clk(CLOCK), .Q(PROGRAM_COUNTER));  // open: en, clr
  Register #(.width(32)) register_1 (.D(INSTRUCTION), .en(1'b0), .clk(CLOCK), .Q(register_1_q));  // open: clr
  immediate_generator immediate_generator_1 (
    .imm(register_1_q[31:7]), .immOut(immediate_generator_1_immout));  // open: ImmSel
  regfile_main RegFile (
    .rs2(register_1_q[24:20]), .rd(register_1_q[11:7]), .Read_Data_1(RegFile_read_data_1),
    .Read_Data_2(RegFile_read_data_2), .ra(ra), .sp(sp), .t0(t0), .t1(t1), .t2(t2), .s0(s0), .s1(s1),
    .a0(a0), .rs1(register_1_q[19:15]), .Write_Data(multiplexer_4_out), .clk(CLOCK));  // open: RegWEn
  Multiplexer #(.width(32), .enable("false")) multiplexer_2 (
    .in0(RegFile_read_data_1), .in1(PROGRAM_COUNTER), .out(multiplexer_2_out));  // open: sel
  Multiplexer #(.width(32), .enable("false")) multiplexer_3 (
    .in0(RegFile_read_data_2), .in1(immediate_generator_1_immout), .out(multiplexer_3_out));  // open: sel
  alu Arithmetic_Logic_Unit (.B(multiplexer_3_out), .Result(alu), .A(multiplexer_2_out));  // open: ALUSel
  // mem_main DMEM: pin names not known; wires that end beside it: DMEM_p1, alu, RegFile_read_data_2, DMEM_p1, CLOCK, DMEM_p6, DMEM_p6, DMEM_p8, DMEM_p9
  Multiplexer #(.select(2), .width(32), .enable("false")) multiplexer_4 (
    .in0(pc_plus_4), .in1(alu), .in2(DMEM_p9), .out(multiplexer_4_out));  // open: in3, sel

  // Other names for the same wires on the sheet: clk = CLOCK

  // Notes on the sheet:
  //   Output
  //   IMEM (do **NOT** move this)
  //   Inputs
  //   Inputs/Outputs for testing. Do **NOT** move these.
endmodule

module control_module (
  input  [31:0] Instruction_32,
  input  BrEq,
  input  BrLt,
  output [1:0] WBSel,
  output ASel,
  output BSel,
  output MemRW,
  output BrUn,
  output RegWEn,
  output [2:0] ImmSel,
  output PCSel,
  output [3:0] ALUSel
);

  wire add, and_1_out, and_2_out, and_3_out, and_4_out, and_5_out, and_6_out, and_7_out, and_8_out,
       and_9_out, and_10_out, and_11_out, and_12_out, and_13_out, and_14_out, and_15_out, and_18_out,
       and_19_out, and_20_out, and_21_out, and_22_out, and_23_out, and_24_out, and_25_out, comparator_1_eq,
       comparator_2_eq, comparator_3_eq, comparator_4_eq, comparator_5_eq, comparator_6_eq, comparator_7_eq,
       comparator_8_eq, comparator_9_eq, comparator_10_eq, comparator_11_eq, comparator_12_eq,
       comparator_13_eq, comparator_14_eq, comparator_15_eq, comparator_16_eq, comparator_17_eq,
       comparator_18_eq, comparator_19_eq, comparator_20_eq, comparator_21_eq, comparator_22_eq,
       comparator_23_eq, comparator_24_eq, comparator_25_eq, comparator_26_eq, comparator_27_eq,
       comparator_28_eq, comparator_29_eq, comparator_30_eq, comparator_31_eq, comparator_32_eq,
       comparator_33_eq, comparator_34_eq, comparator_35_eq, comparator_36_eq, comparator_37_eq,
       comparator_38_eq, comparator_39_eq, comparator_40_eq, comparator_41_eq, comparator_42_eq,
       comparator_43_eq, comparator_44_eq, comparator_45_eq, comparator_46_eq, comparator_47_eq,
       comparator_48_eq, comparator_49_eq, comparator_50_eq, comparator_51_eq, comparator_52_eq,
       comparator_53_eq, comparator_54_eq, comparator_55_eq, isAdd, isMul, isSub, not_1_out, not_3_out,
       not_4_out, not_5_out, not_6_out, not_7_out, not_8_out, not_9_out, not_10_out, not_11_out, not_12_out,
       not_13_out, not_14_out, not_15_out, or_4_out, or_5_out, or_6_out, or_7_out, or_8_out;
  wire [3:0] multiplexer_1_out, multiplexer_2_out, multiplexer_3_out, multiplexer_4_out, multiplexer_5_out,
       multiplexer_6_out, multiplexer_7_out, multiplexer_8_out, multiplexer_9_out, multiplexer_10_out,
       multiplexer_11_out, multiplexer_12_out, multiplexer_13_out, undriven_2;
  wire [16:0] instID;
  wire [31:0] undriven;

  Comparator #(.width(3), .mode("unsigned")) comparator_1 (
    .a(ImmSel), .b(3'b001), .eq(comparator_1_eq));  // open: gt, lt
  Comparator #(.width(10), .mode("unsigned")) comparator_2 (
    .a({Instruction_32[31:25], Instruction_32[14:12]}), .b(10'h11), .eq(comparator_2_eq));  // open: gt, lt
  Comparator #(.width(3), .mode("unsigned")) comparator_3 (
    .a(ImmSel), .b(3'b001), .eq(comparator_3_eq));  // open: gt, lt
  Comparator #(.width(10), .mode("unsigned")) comparator_4 (
    .a({Instruction_32[31:25], Instruction_32[14:12]}), .b({10{1'b0}}), .eq(comparator_4_eq));  // open: gt, lt
  Multiplexer #(.width(4), .enable("false")) multiplexer_1 (
    .in0(4'b1111), .in1(4'b1110), .out(multiplexer_1_out), .sel(and_1_out));
  and and_1 (and_1_out, comparator_1_eq, comparator_2_eq);
  Comparator #(.width(3), .mode("unsigned")) comparator_5 (
    .a(ImmSel), .b(3'b001), .eq(comparator_5_eq));  // open: gt, lt
  Comparator #(.width(10), .mode("unsigned")) comparator_6 (
    .a({Instruction_32[31:25], Instruction_32[14:12]}), .b(10'h200), .eq(comparator_6_eq));  // open: gt, lt
  and and_2 (and_2_out, comparator_3_eq, comparator_4_eq);
  Comparator #(.width(3), .mode("unsigned")) comparator_7 (
    .a(ImmSel), .b(3'b100), .eq(comparator_7_eq));  // open: gt, lt
  Comparator #(.width(3), .mode("unsigned")) comparator_8 (
    .a(Instruction_32[14:12]), .b(3'b000), .eq(comparator_8_eq));  // open: gt, lt
  Comparator #(.width(3), .mode("unsigned")) comparator_9 (
    .a(Instruction_32[14:12]), .b(3'b001), .eq(comparator_9_eq));  // open: gt, lt
  Comparator #(.width(3), .mode("unsigned")) comparator_10 (
    .a(Instruction_32[14:12]), .b(3'b100), .eq(comparator_10_eq));  // open: gt, lt
  Comparator #(.width(3), .mode("unsigned")) comparator_11 (
    .a(Instruction_32[14:12]), .b(3'b110), .eq(comparator_11_eq));  // open: gt, lt
  Multiplexer #(.width(4), .enable("false")) multiplexer_2 (
    .in0(multiplexer_1_out), .in1(4'b1100), .out(multiplexer_2_out), .sel(and_3_out));
  and and_3 (and_3_out, comparator_5_eq, comparator_6_eq);
  Comparator #(.width(3), .mode("unsigned")) comparator_12 (
    .a(ImmSel), .b(3'b001), .eq(comparator_12_eq));  // open: gt, lt
  Comparator #(.width(10), .mode("unsigned")) comparator_13 (
    .a({Instruction_32[31:25], Instruction_32[14:12]}), .b(10'h13), .eq(comparator_13_eq));  // open: gt, lt
  Multiplexer #(.width(4), .enable("false")) multiplexer_3 (
    .in0(multiplexer_2_out), .in1(4'b1011), .out(multiplexer_3_out), .sel(and_4_out));
  and and_4 (and_4_out, comparator_12_eq, comparator_13_eq);
  Comparator #(.width(3), .mode("unsigned")) comparator_14 (
    .a(ImmSel), .b(3'b001), .eq(comparator_14_eq));  // open: gt, lt
  Comparator #(.width(10), .mode("unsigned")) comparator_15 (
    .a({Instruction_32[31:25], Instruction_32[14:12]}), .b(10'h10), .eq(comparator_15_eq));  // open: gt, lt
  Comparator #(.width(3), .mode("unsigned")) comparator_16 (
    .a(ImmSel), .b(3'b001), .eq(comparator_16_eq));  // open: gt, lt
  Comparator #(.width(10), .mode("unsigned")) comparator_17 (
    .a({Instruction_32[31:25], Instruction_32[14:12]}), .b(10'h4), .eq(comparator_17_eq));  // open: gt, lt
  Comparator #(.width(3), .mode("unsigned")) comparator_18 (
    .a(ImmSel), .b(3'b010), .eq(comparator_18_eq));  // open: gt, lt
  Comparator #(.width(3), .mode("unsigned")) comparator_19 (
    .a(Instruction_32[14:12]), .b(3'b000), .eq(comparator_19_eq));  // open: gt, lt
  not not_1 (not_1_out, BrEq);
  Multiplexer #(.width(4), .enable("false")) multiplexer_4 (
    .in0(multiplexer_3_out), .in1(4'b1010), .out(multiplexer_4_out), .sel(and_5_out));
  and and_5 (and_5_out, comparator_14_eq, comparator_15_eq);
  Comparator #(.width(3), .mode("unsigned")) comparator_20 (
    .a(ImmSel), .b(3'b001), .eq(comparator_20_eq));  // open: gt, lt
  Comparator #(.width(10), .mode("unsigned")) comparator_21 (
    .a({Instruction_32[31:25], Instruction_32[14:12]}), .b(10'h17), .eq(comparator_21_eq));  // open: gt, lt
  Comparator #(.width(3), .mode("unsigned")) comparator_22 (
    .a(ImmSel), .b(3'b001), .eq(comparator_22_eq));  // open: gt, lt
  Comparator #(.width(10), .mode("unsigned")) comparator_23 (
    .a({Instruction_32[31:25], Instruction_32[14:12]}), .b(10'h5), .eq(comparator_23_eq));  // open: gt, lt
  and and_6 (and_6_out, comparator_16_eq, comparator_17_eq);
  Comparator #(.width(3), .mode("unsigned")) comparator_24 (
    .a(ImmSel), .b(3'b011), .eq(comparator_24_eq));  // open: gt, lt
  Comparator #(.width(3), .mode("unsigned")) comparator_25 (
    .a(Instruction_32[14:12]), .b(3'b010), .eq(comparator_25_eq));  // open: gt, lt
  Comparator #(.width(3), .mode("unsigned")) comparator_26 (
    .a(ImmSel), .b(3'b100), .eq(comparator_26_eq));  // open: gt, lt
  Comparator #(.width(3), .mode("unsigned")) comparator_27 (
    .a(Instruction_32[14:12]), .b(3'b110), .eq(comparator_27_eq));  // open: gt, lt
  Comparator #(.width(3), .mode("unsigned")) comparator_28 (
    .a(ImmSel), .b(3'b001), .eq(comparator_28_eq));  // open: gt, lt
  Comparator #(.width(3), .mode("unsigned")) comparator_29 (
    .a(ImmSel), .b(3'b010), .eq(comparator_29_eq));  // open: gt, lt
  Comparator #(.width(3), .mode("unsigned")) comparator_30 (
    .a(ImmSel), .b(3'b101), .eq(comparator_30_eq));  // open: gt, lt
  Comparator #(.width(3), .mode("unsigned")) comparator_31 (
    .a(ImmSel), .b(3'b110), .eq(comparator_31_eq));  // open: gt, lt
  Comparator #(.width(3), .mode("unsigned")) comparator_32 (
    .a(ImmSel), .b(3'b110), .eq(comparator_32_eq));  // open: gt, lt
  and and_7 (and_7_out, comparator_18_eq, comparator_19_eq);
  and and_8 (and_8_out, comparator_7_eq, BrEq, comparator_8_eq);
  and and_9 (and_9_out, comparator_7_eq, not_1_out, comparator_9_eq);
  and and_10 (and_10_out, comparator_7_eq, BrLt, comparator_10_eq);
  and and_11 (and_11_out, comparator_7_eq, BrLt, comparator_11_eq);
  Multiplexer #(.width(4), .enable("false")) multiplexer_5 (
    .in0(multiplexer_4_out), .in1(4'b1001), .out(multiplexer_5_out), .sel(and_12_out));
  and and_12 (and_12_out, comparator_20_eq, comparator_21_eq);
  Comparator #(.width(3), .mode("unsigned")) comparator_33 (
    .a(ImmSel), .b(3'b001), .eq(comparator_33_eq));  // open: gt, lt
  Comparator #(.width(10), .mode("unsigned")) comparator_34 (
    .a({Instruction_32[31:25], Instruction_32[14:12]}), .b(10'h15), .eq(comparator_34_eq));  // open: gt, lt
  and and_13 (and_13_out, comparator_22_eq, comparator_23_eq);
  Comparator #(.width(3), .mode("unsigned")) comparator_35 (
    .a(ImmSel), .b(3'b001), .eq(comparator_35_eq));  // open: gt, lt
  Comparator #(.width(10), .mode("unsigned")) comparator_36 (
    .a({Instruction_32[31:25], Instruction_32[14:12]}), .b(10'h6), .eq(comparator_36_eq));  // open: gt, lt
  Comparator #(.width(3), .mode("unsigned")) comparator_37 (
    .a(ImmSel), .b(3'b100), .eq(comparator_37_eq));  // open: gt, lt
  Comparator #(.width(3), .mode("unsigned")) comparator_38 (
    .a(ImmSel), .b(3'b110), .eq(comparator_38_eq));  // open: gt, lt
  Multiplexer #(.width(4), .enable("false")) multiplexer_6 (
    .in0(multiplexer_5_out), .in1(4'b1000), .out(multiplexer_6_out), .sel(and_14_out));
  and and_14 (and_14_out, comparator_33_eq, comparator_34_eq);
  Comparator #(.width(3), .mode("unsigned")) comparator_39 (
    .a(ImmSel), .b(3'b001), .eq(comparator_39_eq));  // open: gt, lt
  Comparator #(.width(10), .mode("unsigned")) comparator_40 (
    .a({Instruction_32[31:25], Instruction_32[14:12]}), .b(10'h2), .eq(comparator_40_eq));  // open: gt, lt
  and and_15 (and_15_out, comparator_35_eq, comparator_36_eq);
  Comparator #(.width(3), .mode("unsigned")) comparator_41 (
    .a(ImmSel), .b(3'b001), .eq(comparator_41_eq));  // open: gt, lt
  Comparator #(.width(10), .mode("unsigned")) comparator_42 (
    .a({Instruction_32[31:25], Instruction_32[14:12]}), .b(10'h7), .eq(comparator_42_eq));  // open: gt, lt
  Comparator #(.width(3), .mode("unsigned")) comparator_43 (
    .a(ImmSel), .b(3'b001), .eq(comparator_43_eq));  // open: gt, lt
  and and_16 (MemRW, comparator_24_eq, comparator_25_eq);
  and and_17 (BrUn, comparator_26_eq, comparator_27_eq);
  or or_1 (RegWEn, comparator_28_eq, comparator_29_eq, comparator_30_eq, comparator_31_eq);
  or or_2 (PCSel, comparator_32_eq, and_7_out, and_8_out, and_9_out, and_10_out, and_11_out);
  Multiplexer #(.width(4), .enable("false")) multiplexer_7 (
    .in0(multiplexer_6_out), .in1(4'b0111), .out(multiplexer_7_out), .sel(and_18_out));
  and and_18 (and_18_out, comparator_39_eq, comparator_40_eq);
  Comparator #(.width(3), .mode("unsigned")) comparator_44 (
    .a(ImmSel), .b(3'b001), .eq(comparator_44_eq));  // open: gt, lt
  Comparator #(.width(10), .mode("unsigned")) comparator_45 (
    .a({Instruction_32[31:25], Instruction_32[14:12]}), .b(10'h1), .eq(comparator_45_eq));  // open: gt, lt
  and and_19 (and_19_out, comparator_41_eq, comparator_42_eq);
  or or_3 (ASel, comparator_37_eq, comparator_38_eq);
  not not_2 (BSel, comparator_43_eq);
  Multiplexer #(.width(4), .enable("false")) multiplexer_8 (
    .in0(multiplexer_7_out), .in1(4'b0110), .out(multiplexer_8_out), .sel(and_20_out));
  and and_20 (and_20_out, comparator_44_eq, comparator_45_eq);
  Comparator #(.width(3), .mode("unsigned")) comparator_46 (
    .a(ImmSel), .b(3'b001), .eq(comparator_46_eq));  // open: gt, lt
  Comparator #(.width(10), .mode("unsigned")) comparator_47 (
    .a({Instruction_32[31:25], Instruction_32[14:12]}), .b(10'h1), .eq(comparator_47_eq));  // open: gt, lt
  Comparator #(.width(3), .mode("unsigned")) comparator_48 (
    .a(ImmSel), .b(3'b010), .eq(comparator_48_eq));  // open: gt, lt
  and and_21 (and_21_out, comparator_48_eq, comparator_49_eq);
  Comparator #(.width(3), .mode("unsigned")) comparator_49 (
    .a(Instruction_32[14:12]), .b(3'b101), .eq(comparator_49_eq));  // open: gt, lt
  Comparator #(.width(3), .mode("unsigned")) comparator_50 (
    .a(ImmSel), .b(3'b010), .eq(comparator_50_eq));  // open: gt, lt
  Comparator #(.width(3), .mode("unsigned")) comparator_51 (
    .a(Instruction_32[14:12]), .b(3'b100), .eq(comparator_51_eq));  // open: gt, lt
  type_determiner type_determiner_1 (.Opcode(Instruction_32[6:0]), .InstrType(ImmSel));
  Multiplexer #(.width(4), .enable("false")) multiplexer_9 (
    .in0(multiplexer_8_out), .in1(4'b0101), .out(multiplexer_9_out), .sel(and_22_out));
  and and_22 (and_22_out, comparator_46_eq, comparator_47_eq);
  and and_23 (and_23_out, comparator_50_eq, comparator_51_eq);
  Multiplexer #(.width(4), .enable("false")) multiplexer_10 (
    .in0(multiplexer_9_out), .in1(4'b0100), .out(multiplexer_10_out), .sel(or_4_out));
  or or_4 (or_4_out, and_13_out, and_21_out);
  Comparator #(.width(3), .mode("unsigned")) comparator_52 (
    .a(ImmSel), .b(3'b010), .eq(comparator_52_eq));  // open: gt, lt
  and and_24 (and_24_out, comparator_52_eq, comparator_53_eq);
  Comparator #(.width(3), .mode("unsigned")) comparator_53 (
    .a(Instruction_32[14:12]), .b(3'b110), .eq(comparator_53_eq));  // open: gt, lt
  Multiplexer #(.width(4), .enable("false")) multiplexer_11 (
    .in0(multiplexer_10_out), .in1(4'b0011), .out(multiplexer_11_out), .sel(or_5_out));
  or or_5 (or_5_out, and_6_out, and_23_out);
  Comparator #(.width(3), .mode("unsigned")) comparator_54 (
    .a(ImmSel), .b(3'b010), .eq(comparator_54_eq));  // open: gt, lt
  and and_25 (and_25_out, comparator_54_eq, comparator_55_eq);
  Comparator #(.width(3), .mode("unsigned")) comparator_55 (
    .a(Instruction_32[14:12]), .b(3'b111), .eq(comparator_55_eq));  // open: gt, lt
  Multiplexer #(.width(4), .enable("false")) multiplexer_12 (
    .in0(multiplexer_11_out), .in1(4'b0010), .out(multiplexer_12_out), .sel(or_6_out));
  or or_6 (or_6_out, and_15_out, and_24_out);
  Multiplexer #(.width(4), .enable("false")) multiplexer_13 (
    .in0(multiplexer_12_out), .in1(4'b0001), .out(multiplexer_13_out), .sel(or_7_out));
  or or_7 (or_7_out, and_19_out, and_25_out);
  Multiplexer #(.width(4), .enable("false")) multiplexer_14 (
    .in0(multiplexer_13_out), .in1(4'b0000), .out(ALUSel), .sel(or_8_out));
  buf or_8 (or_8_out, and_2_out);  // OR_Gate
  not not_3 (not_3_out, undriven[31]);
  not not_4 (not_4_out, undriven[30]);
  not not_5 (not_5_out, undriven[29]);
  not not_6 (not_6_out, undriven[28]);
  not not_7 (not_7_out, undriven[27]);
  not not_8 (not_8_out, undriven[26]);
  not not_9 (not_9_out, undriven[25]);
  not not_10 (not_10_out, undriven[14]);
  not not_11 (not_11_out, undriven[13]);
  and and_26 (add, not_3_out, not_4_out, not_5_out, not_6_out, not_7_out, not_8_out, not_9_out, not_10_out, not_11_out, not_12_out, not_13_out, undriven[5], undriven[4], not_14_out, not_15_out, undriven[1], undriven[0]);
  not not_12 (not_12_out, undriven[12]);
  not not_13 (not_13_out, undriven[6]);
  not not_14 (not_14_out, undriven[3]);
  not not_15 (not_15_out, undriven[2]);
  Multiplexer #(.width(4), .enable("false")) multiplexer_15 (.in0(undriven_2), .in1(4'b1101));  // open: out, sel
  Comparator #(.width(17), .mode("unsigned")) comparator_56 (.a(instID), .b({17{1'b0}}), .eq(isAdd));  // open: gt, lt
  Comparator #(.width(17), .mode("unsigned")) comparator_57 (.a(instID), .b({17{1'b0}}), .eq(isMul));  // open: gt, lt
  Comparator #(.width(17), .mode("unsigned")) comparator_58 (.a(instID), .b({17{1'b0}}), .eq(isSub));  // open: gt, lt

  // Other names for the same wires on the sheet: inst_type[2:0] = ImmSel; instID_I_S_SB[2:0] = Instruction_32[14:12];
  //   instID_R[9:0] = {Instruction_32[31:25], Instruction_32[14:12]}; instID_U_UJ[6:0] = Instruction_32[6:0]

  // Notes on the sheet:
  //   mulh
  //   add
  //   error_indicator
  //   sub
  //   beq
  //   bne
  //   blt
  //   bltu
  //   Mulh?
  //   mulhu
  //   Sub?
  //   mul
  //   Type Determiner
  //   jalr
  //   Mulhu?
  //   remu
  //   xor
  //   Mul?
  //   divu
  //   srl
  //   or
  //   R-func7func3
  //   sw
  //   bltu
  //   Remu?
  //   slt
  //   opcode
  //   I/S/SB(B)-func3
  //   Divu?
  //   sll
  //   and
  //   U/UJ(J)-opcode
  //   Slt?
  //   ??
  //   srli
  //   Sll?
  //   xori
  //   Sra?
  //   FIX
  //   ori
  //   Srl?
  //   andi
  //   Xor?
  //   Or?
  //   And?
  //   Add?
  //   Bsel?
endmodule

module immediate_generator (
  input  [2:0] ImmSel,
  input  [24:0] imm,
  output [31:0] immOut
);

  wire [31:0] i, s, sb, uj;

  assign i = {{20{imm[24]}}, imm[24:13]};  // Bit_Extender bit_extender_1
  assign s = {{20{imm[24]}}, {imm[24:18], imm[4:0]}};  // Bit_Extender bit_extender_2
  assign sb = {{19{imm[24]}}, {imm[24], imm[0], imm[23:18], imm[4:1], 1'b0}};  // Bit_Extender bit_extender_3
  assign uj = {{11{imm[24]}}, {imm[24], imm[12:5], imm[13], imm[23:14], 1'b0}};  // Bit_Extender bit_extender_4
  Multiplexer #(.select(3), .width(32), .enable("false")) multiplexer_1 (
    .in1({32{1'b1}}), .in2(i), .in3(s), .in4(sb), .in5({imm[24:5], {12{1'b0}}}), .in6(uj), .out(immOut),
    .sel(ImmSel));  // open: in0, in7

  // Other names for the same wires on the sheet: immIn[24:0] = imm; u[31:12] = imm[24:5]
endmodule

module type_determiner (
  input  [6:0] Opcode,
  output [2:0] InstrType
);

  wire comparator_1_eq, comparator_2_eq, comparator_3_eq, comparator_4_eq, comparator_5_eq, comparator_6_eq,
       comparator_7_eq, comparator_8_eq, or_1_out;
  wire [3:0] adder_1_out, adder_2_out, adder_3_out, adder_4_out, multiplexer_1_out, multiplexer_2_out,
       multiplexer_3_out, multiplexer_4_out, multiplexer_5_out, multiplexer_6_out;
  wire [3:3] adder_5_out;

  Comparator #(.width(7), .mode("unsigned")) comparator_1 (
    .a(Opcode), .b(7'b0110011), .eq(comparator_1_eq));  // open: gt, lt
  Comparator #(.width(7), .mode("unsigned")) comparator_2 (
    .a(Opcode), .b(7'b0000011), .eq(comparator_2_eq));  // open: gt, lt
  Comparator #(.width(7), .mode("unsigned")) comparator_3 (
    .a(Opcode), .b(7'b0010011), .eq(comparator_3_eq));  // open: gt, lt
  Comparator #(.width(7), .mode("unsigned")) comparator_4 (
    .a(Opcode), .b(7'b1100111), .eq(comparator_4_eq));  // open: gt, lt
  Comparator #(.width(7), .mode("unsigned")) comparator_5 (
    .a(Opcode), .b(7'b0100011), .eq(comparator_5_eq));  // open: gt, lt
  Comparator #(.width(7), .mode("unsigned")) comparator_6 (
    .a(Opcode), .b(7'b1100011), .eq(comparator_6_eq));  // open: gt, lt
  Comparator #(.width(7), .mode("unsigned")) comparator_7 (
    .a(Opcode), .b(7'b0110111), .eq(comparator_7_eq));  // open: gt, lt
  Comparator #(.width(7), .mode("unsigned")) comparator_8 (
    .a(Opcode), .b(7'b1101111), .eq(comparator_8_eq));  // open: gt, lt
  Multiplexer #(.width(4), .enable("false")) multiplexer_1 (
    .in0(4'b0000), .in1(4'b0001), .out(multiplexer_1_out), .sel(comparator_1_eq));
  or or_1 (or_1_out, comparator_2_eq, comparator_3_eq, comparator_4_eq);
  Multiplexer #(.width(4), .enable("false")) multiplexer_2 (
    .in0(4'b0000), .in1(4'b0011), .out(multiplexer_2_out), .sel(comparator_5_eq));
  Multiplexer #(.width(4), .enable("false")) multiplexer_3 (
    .in0(4'b0000), .in1(4'b0010), .out(multiplexer_3_out), .sel(or_1_out));
  Multiplexer #(.width(4), .enable("false")) multiplexer_4 (
    .in0(4'b0000), .in1(4'b0100), .out(multiplexer_4_out), .sel(comparator_6_eq));
  Multiplexer #(.width(4), .enable("false")) multiplexer_5 (
    .in0(4'b0000), .in1(4'b0101), .out(multiplexer_5_out), .sel(comparator_7_eq));
  Multiplexer #(.width(4), .enable("false")) multiplexer_6 (
    .in0(4'b0000), .in1(4'b0110), .out(multiplexer_6_out), .sel(comparator_8_eq));
  Adder #(.width(4)) adder_1 (.a(multiplexer_1_out), .b(multiplexer_3_out), .out(adder_1_out));  // open: cin, cout
  Adder #(.width(4)) adder_2 (.a(adder_1_out), .b(multiplexer_2_out), .out(adder_2_out));  // open: cin, cout
  Adder #(.width(4)) adder_3 (.a(adder_2_out), .b(multiplexer_4_out), .out(adder_3_out));  // open: cin, cout
  Adder #(.width(4)) adder_4 (.a(adder_3_out), .b(multiplexer_5_out), .out(adder_4_out));  // open: cin, cout
  Adder #(.width(4)) adder_5 (
    .a(adder_4_out), .b(multiplexer_6_out), .out({adder_5_out[3], InstrType}));  // open: cin, cout

  // Notes on the sheet:
  //   R
  //   I
  //   S
  //   SB
  //   U
  //   UJ
endmodule

module branch_comp (
  input  [31:0] rs1,
  input  [31:0] rs2,
  input  BrUn,
  output BrEq,
  output BrLT
);

  wire comparator_1_eq, comparator_2_eq, comparator_3_lt, comparator_4_lt;

  Comparator #(.width(32)) comparator_1 (.a(rs1), .b(rs2), .eq(comparator_1_eq));  // open: gt, lt
  Comparator #(.width(32), .mode("unsigned")) comparator_2 (.a(rs1), .b(rs2), .eq(comparator_2_eq));  // open: gt, lt
  Comparator #(.width(32)) comparator_3 (.a(rs1), .b(rs2), .lt(comparator_3_lt));  // open: gt, eq
  Comparator #(.width(32), .mode("unsigned")) comparator_4 (.a(rs1), .b(rs2), .lt(comparator_4_lt));  // open: gt, eq
  Multiplexer #(.enable("false")) multiplexer_1 (.in0(comparator_1_eq), .in1(comparator_2_eq), .out(BrEq), .sel(BrUn));
  Multiplexer #(.enable("false")) multiplexer_2 (.in0(comparator_3_lt), .in1(comparator_4_lt), .out(BrLT), .sel(BrUn));

  // Other names for the same wires on the sheet: A[31:0] = rs1; B[31:0] = rs2
endmodule
